// Logisim project CPU_8_bit.circ as structural Verilog: 13 circuits, main circuit CPU_8bit
module CPU_8bit (
  input  program_mode,
  input  pclk,
  input  rst,
  input  [3:0] progam_addr,
  input  [7:0] program_mem,
  output out_6,
  output out_7,
  output out_8,
  output out_9,
  output out_10,
  output out_11,
  output out_12,
  output out_13,
  output out_14,
  output out_15,
  output out_16,
  output out_17,
  output out_18,
  output out_19,
  output out_20,
  output out_21
);

  wire alu_1_carry_bit, and_1_out, clk_out, controller_1_aluin, controller_1_aluout, controller_1_aregin,
       controller_1_aregout, controller_1_bregin, controller_1_hltclk, controller_1_irin, controller_1_irout,
       controller_1_jmpen, controller_1_marin, controller_1_outregin, controller_1_pcount_en,
       controller_1_pcout, controller_1_ramin, controller_1_ramout, instructionregister_1_opcode_0,
       instructionregister_1_opcode_1, instructionregister_1_opcode_2, instructionregister_1_opcode_3,
       mar_1_addr_0, mar_1_addr_1, mar_1_addr_2, mar_1_addr_3, not_1_out, or_1_out;
  wire [7:0] a_reg_1_a_alu0, b_reg_1_b_out_0;

  Clock clk (.out(clk_out));
  or or_1 (or_1_out, pclk, and_1_out);
  not not_1 (not_1_out, controller_1_hltclk);
  and and_1 (and_1_out, clk_out, not_1_out);
  Controller controller_1 (
    .clk(and_1_out), .op3(instructionregister_1_opcode_3), .op2(instructionregister_1_opcode_2),
    .op1(instructionregister_1_opcode_1), .op0(instructionregister_1_opcode_0), .PCout(controller_1_pcout),
    .MARin(controller_1_marin), .RAMout(controller_1_ramout), .IRin(controller_1_irin),
    .PCount_en(controller_1_pcount_en), .ALUin(controller_1_aluin), .OUTREGin(controller_1_outregin),
    .AREGin(controller_1_aregin), .ALUout(controller_1_aluout), .AREGout(controller_1_aregout),
    .HLTclk(controller_1_hltclk), .BREGin(controller_1_bregin), .IRout(controller_1_irout), .rst(rst),
    .program_mode(program_mode), .RAMin(controller_1_ramin), .JMPen(controller_1_jmpen),
    .carry_bit(alu_1_carry_bit));
  MAR mar_1 (
    .din_3(out_10), .pin_3(progam_addr[3]), .din_2(out_11), .pin_2(progam_addr[2]), .din_1(out_12),
    .pin_1(progam_addr[1]), .din_0(out_13), .pin_0(progam_addr[0]), .addr_3(mar_1_addr_3),
    .addr_2(mar_1_addr_2), .addr_1(mar_1_addr_1), .addr_0(mar_1_addr_0), .clk(or_1_out),
    .en(controller_1_marin), .program_mode(program_mode));
  RAM_16byte ram_16byte_1 (
    .addr_3(mar_1_addr_3), .addr_2(mar_1_addr_2), .addr_1(mar_1_addr_1), .program_mode(program_mode),
    .addr_0(mar_1_addr_0), .write(controller_1_ramin), .clk(or_1_out), .pin_7(program_mem[7]), .out_7(out_6),
    .pin_6(program_mem[6]), .out_6(out_7), .pin_5(program_mem[5]), .out_5(out_8), .pin_4(program_mem[4]),
    .out_4(out_9), .pin_3(program_mem[3]), .out_3(out_10), .pin_2(program_mem[2]), .out_2(out_11),
    .pin_1(program_mem[1]), .out_1(out_12), .pin_0(program_mem[0]), .out_0(out_13), .read(controller_1_ramout));
  InstructionRegister instructionregister_1 (
    .clk(and_1_out), .ir_en(controller_1_irin), .ir_out_0(out_13), .ir_out_1(out_12), .ir_out_2(out_11),
    .ir_out_3(out_10), .ir_out_4(out_9), .ir_out_5(out_8), .ir_out_6(out_7), .ir_out_7(out_6),
    .ir_out(controller_1_irout), .opCode_0(instructionregister_1_opcode_0),
    .opCode_1(instructionregister_1_opcode_1), .opCode_2(instructionregister_1_opcode_2),
    .opCode_3(instructionregister_1_opcode_3), .bin0(out_13), .iin1(out_12), .iin2(out_11), .iin3(out_10),
    .iin4(out_9), .iin5(out_8), .iin6(out_7), .iin7(out_6));
  ProgramCounter programcounter_1 (
    .out_en(controller_1_pcout), .clk(and_1_out), .count_en(controller_1_pcount_en),
    .jump(controller_1_jmpen), .pc_0(out_13), .pc_1(out_12), .pc_2(out_11), .pc_3(out_10), .rst(rst),
    .jin_0(out_13), .jin_1(out_12), .jin_3(out_10), .jin_2(out_11));
  ALU alu_1 (
    .clk(and_1_out), .alu_in(controller_1_aluin), .ALU_out(controller_1_aluout), .A(a_reg_1_a_alu0),
    .B(b_reg_1_b_out_0), .ALU_0(out_13), .ALU_1(out_12), .ALU_2(out_11), .ALU_3(out_10), .ALU_4(out_9),
    .ALU_5(out_8), .ALU_6(out_7), .ALU_7(out_6), .cmd_2(out_7), .cmd_1(out_8), .cmd_0(out_9),
    .carry_bit(alu_1_carry_bit));
  A_reg a_reg_1 (
    .a_out_en(controller_1_aregout), .clk(and_1_out), .a_en(controller_1_aregin), .a_out_0(out_13),
    .a_out_1(out_12), .a_out_2(out_11), .a_out_3(out_10), .a_out_4(out_9), .a_out_5(out_8), .a_out_6(out_7),
    .a_out_7(out_6), .a_alu3(a_reg_1_a_alu0[3]), .a_alu2(a_reg_1_a_alu0[2]), .a_alu0(a_reg_1_a_alu0[0]),
    .a_alu1(a_reg_1_a_alu0[1]), .a_alu4(a_reg_1_a_alu0[4]), .a_alu5(a_reg_1_a_alu0[5]),
    .a_alu6(a_reg_1_a_alu0[6]), .a_alu7(a_reg_1_a_alu0[7]), .ain7(out_6), .ain6(out_7), .ain5(out_8),
    .ain4(out_9), .ain3(out_10), .ain2(out_11), .ain1(out_12), .ain0(out_13), .in_12(rst));
  B_reg b_reg_1 (
    .clk(and_1_out), .b_en(controller_1_bregin), .b_out_0(b_reg_1_b_out_0[0]), .b_out_1(b_reg_1_b_out_0[1]),
    .b_out_2(b_reg_1_b_out_0[2]), .b_out_3(b_reg_1_b_out_0[3]), .b_out_4(b_reg_1_b_out_0[4]),
    .b_out_5(b_reg_1_b_out_0[5]), .b_out_6(b_reg_1_b_out_0[6]), .b_out_7(b_reg_1_b_out_0[7]), .bin7(out_6),
    .bin6(out_7), .bin5(out_8), .bin4(out_9), .bin3(out_10), .bin2(out_11), .bin1(out_12), .bin0(out_13),
    .rst(rst));
  Out_reg out_reg_1 (
    .clk(and_1_out), .out_en(controller_1_outregin), .out_0(out_21), .out_1(out_20), .out_2(out_19),
    .out_3(out_18), .out_4(out_17), .out_5(out_16), .out_6(out_15), .out_7(out_14), .in7(out_6), .in6(out_7),
    .in5(out_8), .in4(out_9), .in3(out_10), .in2(out_11), .in1(out_12), .in0(out_13), .in_11(rst));
endmodule

module ALU (
  input  cmd_2,
  input  cmd_1,
  input  cmd_0,
  input  clk,
  input  alu_in,
  input  ALU_out,
  input  [7:0] A,
  input  [7:0] B,
  output ALU_0,
  output ALU_1,
  output ALU_2,
  output ALU_3,
  output ALU_4,
  output ALU_5,
  output ALU_6,
  output ALU_7,
  output carry_bit
);

  wire and_1_out, and_3_out, and_4_out, and_5_out, and_6_out, and_7_out, and_8_out, and_9_out, and_10_out,
       and_11_out, and_12_out, and_13_out, and_14_out, and_15_out, and_16_out, and_17_out, and_18_out,
       d_ff_1_q, or_2_out, or_3_out, or_4_out, or_5_out, or_6_out, or_7_out, or_8_out, xor_1_out, xor_2_out,
       xor_3_out, xor_4_out, xor_5_out, xor_6_out, xor_7_out, xor_8_out;
  wire [1:0] d_ff_3_q;
  wire [7:0] and_2_out, multiplexer_1_out, multiplexer_2_out, not_1_out, not_2_out, or_1_out, xor_9_out;

  and and_1 (and_1_out, clk, alu_in);
  D_Flip_Flop d_ff_1 (.D(cmd_2), .clk(and_1_out), .Q(d_ff_1_q));  // open: Qn, preset, reset
  assign not_1_out = ~A;  // NOT_Gate not_1, 8 bits wide
  D_Flip_Flop d_ff_2 (.D(cmd_1), .clk(and_1_out), .Q(d_ff_3_q[1]));  // open: Qn, preset, reset
  Multiplexer #(.width(8), .enable("false")) multiplexer_1 (
    .in0(A), .in1(not_1_out), .out(multiplexer_1_out), .sel(d_ff_1_q));
  D_Flip_Flop d_ff_3 (.D(cmd_0), .clk(and_1_out), .Q(d_ff_3_q[0]));  // open: Qn, preset, reset
  assign and_2_out = multiplexer_1_out & B;  // AND_Gate and_2, 8 bits wide
  assign or_1_out = multiplexer_1_out | B;  // OR_Gate or_1, 8 bits wide
  assign not_2_out = ~B;  // NOT_Gate not_2, 8 bits wide
  xor xor_1 (xor_1_out, multiplexer_1_out[0], B[0]);
  and and_3 (and_3_out, B[0], multiplexer_1_out[0]);
  xor xor_2 (xor_2_out, multiplexer_1_out[1], B[1]);
  and and_4 (and_4_out, B[1], multiplexer_1_out[1]);
  xor xor_3 (xor_3_out, multiplexer_1_out[2], B[2]);
  and and_5 (and_5_out, B[2], multiplexer_1_out[2]);
  xor xor_4 (xor_4_out, multiplexer_1_out[3], B[3]);
  and and_6 (and_6_out, B[3], multiplexer_1_out[3]);
  xor xor_5 (xor_5_out, multiplexer_1_out[4], B[4]);
  and and_7 (and_7_out, B[4], multiplexer_1_out[4]);
  xor xor_6 (xor_6_out, multiplexer_1_out[5], B[5]);
  and and_8 (and_8_out, B[5], multiplexer_1_out[5]);
  xor xor_7 (xor_7_out, multiplexer_1_out[6], B[6]);
  and and_9 (and_9_out, B[6], multiplexer_1_out[6]);
  xor xor_8 (xor_8_out, multiplexer_1_out[7], B[7]);
  and and_10 (and_10_out, B[7], multiplexer_1_out[7]);
  xor xor_9 (xor_9_out[0], xor_1_out, d_ff_1_q);
  and and_11 (and_11_out, xor_1_out, d_ff_1_q);
  or or_2 (or_2_out, and_11_out, and_3_out);
  xor xor_10 (xor_9_out[1], xor_2_out, or_2_out);
  and and_12 (and_12_out, xor_2_out, or_2_out);
  or or_3 (or_3_out, and_12_out, and_4_out);
  xor xor_11 (xor_9_out[2], xor_3_out, or_3_out);
  and and_13 (and_13_out, xor_3_out, or_3_out);
  or or_4 (or_4_out, and_13_out, and_5_out);
  xor xor_12 (xor_9_out[3], xor_4_out, or_4_out);
  and and_14 (and_14_out, xor_4_out, or_4_out);
  or or_5 (or_5_out, and_14_out, and_6_out);
  xor xor_13 (xor_9_out[4], xor_5_out, or_5_out);
  and and_15 (and_15_out, xor_5_out, or_5_out);
  or or_6 (or_6_out, and_15_out, and_7_out);
  xor xor_14 (xor_9_out[5], xor_6_out, or_6_out);
  and and_16 (and_16_out, xor_6_out, or_6_out);
  or or_7 (or_7_out, and_16_out, and_8_out);
  xor xor_15 (xor_9_out[6], xor_7_out, or_7_out);
  and and_17 (and_17_out, xor_7_out, or_7_out);
  or or_8 (or_8_out, and_17_out, and_9_out);
  xor xor_16 (xor_9_out[7], xor_8_out, or_8_out);
  and and_18 (and_18_out, xor_8_out, or_8_out);
  or or_9 (carry_bit, and_18_out, and_10_out);
  assign {ALU_7, ALU_6, ALU_5, ALU_4, ALU_3, ALU_2, ALU_1, ALU_0} = ALU_out ? multiplexer_2_out : 8'bz;  // Controlled_Buffer controlled_buffer_1
  Multiplexer #(.select(2), .width(8), .enable("false")) multiplexer_2 (
    .in0(and_2_out), .in1(xor_9_out), .in2(or_1_out), .in3(not_2_out), .out(multiplexer_2_out), .sel(d_ff_3_q));
endmodule

module A_reg (
  input  a_out_en,
  input  clk,
  input  a_en,
  input  ain7,
  input  ain6,
  input  ain5,
  input  ain4,
  input  ain3,
  input  ain2,
  input  ain1,
  input  ain0,
  input  in_12,
  output a_alu0,
  output a_out_0,
  output a_alu1,
  output a_out_1,
  output a_alu2,
  output a_out_2,
  output a_alu3,
  output a_out_3,
  output a_alu4,
  output a_out_4,
  output a_alu5,
  output a_out_5,
  output a_alu6,
  output a_out_6,
  output a_alu7,
  output a_out_7
);

  wire and_1_out;

  and and_1 (and_1_out, clk, a_en);
  D_Flip_Flop d_ff_1 (.D(ain0), .clk(and_1_out), .Q(a_alu0), .reset(in_12));  // open: Qn, preset
  D_Flip_Flop d_ff_2 (.D(ain1), .clk(and_1_out), .Q(a_alu1), .reset(in_12));  // open: Qn, preset
  D_Flip_Flop d_ff_3 (.D(ain2), .clk(and_1_out), .Q(a_alu2), .reset(in_12));  // open: Qn, preset
  D_Flip_Flop d_ff_4 (.D(ain3), .clk(and_1_out), .Q(a_alu3), .reset(in_12));  // open: Qn, preset
  D_Flip_Flop d_ff_5 (.D(ain4), .clk(and_1_out), .Q(a_alu4), .reset(in_12));  // open: Qn, preset
  D_Flip_Flop d_ff_6 (.D(ain5), .clk(and_1_out), .Q(a_alu5), .reset(in_12));  // open: Qn, preset
  D_Flip_Flop d_ff_7 (.D(ain6), .clk(and_1_out), .Q(a_alu6), .reset(in_12));  // open: Qn, preset
  D_Flip_Flop d_ff_8 (.D(ain7), .clk(and_1_out), .Q(a_alu7), .reset(in_12));  // open: Qn, preset
  assign a_out_0 = a_out_en ? a_alu0 : 1'bz;  // Controlled_Buffer controlled_buffer_1
  assign a_out_1 = a_out_en ? a_alu1 : 1'bz;  // Controlled_Buffer controlled_buffer_2
  assign a_out_2 = a_out_en ? a_alu2 : 1'bz;  // Controlled_Buffer controlled_buffer_3
  assign a_out_3 = a_out_en ? a_alu3 : 1'bz;  // Controlled_Buffer controlled_buffer_4
  assign a_out_4 = a_out_en ? a_alu4 : 1'bz;  // Controlled_Buffer controlled_buffer_5
  assign a_out_5 = a_out_en ? a_alu5 : 1'bz;  // Controlled_Buffer controlled_buffer_6
  assign a_out_6 = a_out_en ? a_alu6 : 1'bz;  // Controlled_Buffer controlled_buffer_7
  assign a_out_7 = a_out_en ? a_alu7 : 1'bz;  // Controlled_Buffer controlled_buffer_8
endmodule

module B_reg (
  input  clk,
  input  b_en,
  input  bin7,
  input  bin6,
  input  bin5,
  input  bin4,
  input  bin3,
  input  bin2,
  input  bin1,
  input  bin0,
  input  rst,
  output b_out_0,
  output b_out_1,
  output b_out_2,
  output b_out_3,
  output b_out_4,
  output b_out_5,
  output b_out_6,
  output b_out_7
);

  wire and_1_out;

  and and_1 (and_1_out, clk, b_en);
  D_Flip_Flop d_ff_1 (.D(bin0), .clk(and_1_out), .Q(b_out_0), .reset(rst));  // open: Qn, preset
  D_Flip_Flop d_ff_2 (.D(bin1), .clk(and_1_out), .Q(b_out_1), .reset(rst));  // open: Qn, preset
  D_Flip_Flop d_ff_3 (.D(bin2), .clk(and_1_out), .Q(b_out_2), .reset(rst));  // open: Qn, preset
  D_Flip_Flop d_ff_4 (.D(bin3), .clk(and_1_out), .Q(b_out_3), .reset(rst));  // open: Qn, preset
  D_Flip_Flop d_ff_5 (.D(bin4), .clk(and_1_out), .Q(b_out_4), .reset(rst));  // open: Qn, preset
  D_Flip_Flop d_ff_6 (.D(bin5), .clk(and_1_out), .Q(b_out_5), .reset(rst));  // open: Qn, preset
  D_Flip_Flop d_ff_7 (.D(bin6), .clk(and_1_out), .Q(b_out_6), .reset(rst));  // open: Qn, preset
  D_Flip_Flop d_ff_8 (.D(bin7), .clk(and_1_out), .Q(b_out_7), .reset(rst));  // open: Qn, preset
endmodule

module ProgramCounter (
  input  out_en,
  input  clk,
  input  count_en,
  input  rst,
  input  jump,
  input  jin_0,
  input  jin_1,
  input  jin_2,
  input  jin_3,
  output pc_0,
  output pc_1,
  output pc_2,
  output pc_3
);

  wire and_1_out, and_2_out, and_3_out, and_4_out, and_5_out, and_6_out, and_7_out, and_8_out, and_9_out,
       d_ff_1_q, d_ff_1_qn, d_ff_2_q, d_ff_2_qn, d_ff_3_q, d_ff_3_qn, d_ff_4_q, d_ff_4_qn, not_1_out,
       not_2_out, not_3_out, not_4_out, or_1_out, or_2_out, or_3_out, or_4_out;

  and and_1 (and_1_out, clk, count_en);
  assign pc_0 = out_en ? d_ff_1_q : 1'bz;  // Controlled_Buffer controlled_buffer_1
  D_Flip_Flop d_ff_1 (
    .D(d_ff_1_qn), .clk(and_1_out), .Q(d_ff_1_q), .Qn(d_ff_1_qn), .preset(and_2_out), .reset(or_1_out));
  or or_1 (or_1_out, rst, and_3_out);
  and and_2 (and_2_out, jump, jin_0);
  and and_3 (and_3_out, jump, not_1_out);
  not not_1 (not_1_out, jin_0);
  D_Flip_Flop d_ff_2 (
    .D(d_ff_2_qn), .clk(d_ff_1_qn), .Q(d_ff_2_q), .Qn(d_ff_2_qn), .preset(and_5_out), .reset(or_2_out));
  or or_2 (or_2_out, rst, and_4_out);
  and and_4 (and_4_out, jump, not_2_out);
  not not_2 (not_2_out, jin_1);
  assign pc_1 = out_en ? d_ff_2_q : 1'bz;  // Controlled_Buffer controlled_buffer_2
  D_Flip_Flop d_ff_3 (
    .D(d_ff_3_qn), .clk(d_ff_2_qn), .Q(d_ff_3_q), .Qn(d_ff_3_qn), .preset(and_6_out), .reset(or_3_out));
  or or_3 (or_3_out, rst, and_7_out);
  and and_5 (and_5_out, jump, jin_1);
  assign pc_2 = out_en ? d_ff_3_q : 1'bz;  // Controlled_Buffer controlled_buffer_3
  and and_6 (and_6_out, jump, jin_2);
  and and_7 (and_7_out, jump, not_3_out);
  not not_3 (not_3_out, jin_2);
  assign pc_3 = out_en ? d_ff_4_q : 1'bz;  // Controlled_Buffer controlled_buffer_4
  D_Flip_Flop d_ff_4 (
    .D(d_ff_4_qn), .clk(d_ff_3_qn), .Q(d_ff_4_q), .Qn(d_ff_4_qn), .preset(and_9_out), .reset(or_4_out));
  or or_4 (or_4_out, rst, and_8_out);
  and and_8 (and_8_out, jump, not_4_out);
  not not_4 (not_4_out, jin_3);
  and and_9 (and_9_out, jump, jin_3);

  // Notes on the sheet:
  //   The output of the program counter will connect to the bus. For this reason we can tie the outputs of the program counter to the load bits
endmodule

module RAM_16byte (
  input  read,
  input  program_mode,
  input  pin_7,
  input  pin_6,
  input  pin_5,
  input  pin_4,
  input  pin_3,
  input  pin_2,
  input  pin_1,
  input  pin_0,
  input  write,
  input  addr_3,
  input  addr_2,
  input  addr_1,
  input  addr_0,
  input  clk,
  output out_7,
  output out_6,
  output out_5,
  output out_4,
  output out_3,
  output out_2,
  output out_1,
  output out_0
);

  wire and_1_out, and_2_out, and_3_out, and_4_out, and_5_out, and_6_out, and_7_out, and_8_out, and_9_out,
       and_10_out, and_11_out, and_12_out, and_13_out, and_14_out, and_15_out, and_16_out, and_17_out,
       and_18_out, and_19_out, and_20_out, and_21_out, and_22_out, and_23_out, and_24_out, and_25_out,
       and_26_out, and_27_out, and_28_out, and_29_out, and_30_out, and_31_out, and_32_out, en0_out, en1_out,
       en2_out, en3_out, en4_out, en5_out, en6_out, en7_out, en8_out, en9_out, en10_out, en11_out, en12_out,
       en13_out, en14_out, en15_out, membit_1_dataout, membit_2_dataout, membit_3_dataout, membit_4_dataout,
       membit_5_dataout, membit_6_dataout, membit_7_dataout, membit_8_dataout, membit_9_dataout,
       membit_10_dataout, membit_11_dataout, membit_12_dataout, membit_13_dataout, membit_14_dataout,
       membit_15_dataout, membit_16_dataout, membit_17_dataout, membit_18_dataout, membit_19_dataout,
       membit_20_dataout, membit_21_dataout, membit_22_dataout, membit_23_dataout, membit_24_dataout,
       membit_25_dataout, membit_26_dataout, membit_27_dataout, membit_28_dataout, membit_29_dataout,
       membit_30_dataout, membit_31_dataout, membit_32_dataout, membit_33_dataout, membit_34_dataout,
       membit_35_dataout, membit_36_dataout, membit_37_dataout, membit_38_dataout, membit_39_dataout,
       membit_40_dataout, membit_41_dataout, membit_42_dataout, membit_43_dataout, membit_44_dataout,
       membit_45_dataout, membit_46_dataout, membit_47_dataout, membit_48_dataout, membit_49_dataout,
       membit_50_dataout, membit_51_dataout, membit_52_dataout, membit_53_dataout, membit_54_dataout,
       membit_55_dataout, membit_56_dataout, membit_57_dataout, membit_58_dataout, membit_59_dataout,
       membit_60_dataout, membit_61_dataout, membit_62_dataout, membit_63_dataout, membit_64_dataout,
       membit_65_dataout, membit_66_dataout, membit_67_dataout, membit_68_dataout, membit_69_dataout,
       membit_70_dataout, membit_71_dataout, membit_72_dataout, membit_73_dataout, membit_74_dataout,
       membit_75_dataout, membit_76_dataout, membit_77_dataout, membit_78_dataout, membit_79_dataout,
       membit_80_dataout, membit_81_dataout, membit_82_dataout, membit_83_dataout, membit_84_dataout,
       membit_85_dataout, membit_86_dataout, membit_87_dataout, membit_88_dataout, membit_89_dataout,
       membit_90_dataout, membit_91_dataout, membit_92_dataout, membit_93_dataout, membit_94_dataout,
       membit_95_dataout, membit_96_dataout, membit_97_dataout, membit_98_dataout, membit_99_dataout,
       membit_100_dataout, membit_101_dataout, membit_102_dataout, membit_103_dataout, membit_104_dataout,
       membit_105_dataout, membit_106_dataout, membit_107_dataout, membit_108_dataout, membit_109_dataout,
       membit_110_dataout, membit_111_dataout, membit_112_dataout, membit_113_dataout, membit_114_dataout,
       membit_115_dataout, membit_116_dataout, membit_117_dataout, membit_118_dataout, membit_119_dataout,
       membit_120_dataout, membit_121_dataout, membit_122_dataout, membit_123_dataout, membit_124_dataout,
       membit_125_dataout, membit_126_dataout, membit_127_dataout, membit_128_dataout, not_1_out, not_2_out,
       not_3_out, not_4_out, not_5_out, or_1_out, or_2_out, or_3_out, or_4_out, or_5_out, or_6_out, or_7_out,
       or_8_out, or_9_out, or_10_out, or_11_out, or_12_out, or_13_out, or_14_out, or_15_out, or_16_out,
       or_17_out, or_18_out;

  not not_1 (not_1_out, addr_3);
  not not_2 (not_2_out, addr_1);
  not not_3 (not_3_out, addr_2);
  or or_1 (or_1_out, program_mode, write);
  not not_4 (not_4_out, addr_0);
  not not_5 (not_5_out, program_mode);
  and en0 (en0_out, not_4_out, not_2_out, not_3_out, not_1_out);
  and en1 (en1_out, addr_0, not_2_out, not_3_out, not_1_out);
  and en2 (en2_out, not_4_out, addr_1, not_3_out, not_1_out);
  and en3 (en3_out, addr_0, addr_1, not_3_out, not_1_out);
  and en4 (en4_out, not_4_out, not_2_out, addr_2, not_1_out);
  and en5 (en5_out, addr_0, not_2_out, addr_2, not_1_out);
  and en6 (en6_out, not_4_out, addr_1, addr_2, not_1_out);
  and en7 (en7_out, addr_0, addr_1, addr_2, not_1_out);
  and en8 (en8_out, not_4_out, not_2_out, not_3_out, addr_3);
  and en9 (en9_out, addr_0, not_2_out, not_3_out, addr_3);
  and en10 (en10_out, not_4_out, addr_1, not_3_out, addr_3);
  and en11 (en11_out, addr_0, addr_1, not_3_out, addr_3);
  and en12 (en12_out, not_4_out, not_2_out, addr_2, addr_3);
  and en13 (en13_out, addr_0, not_2_out, addr_2, addr_3);
  and en14 (en14_out, not_4_out, addr_1, addr_2, addr_3);
  and en15 (en15_out, addr_0, addr_1, addr_2, addr_3);
  or or_2 (or_2_out, program_mode, read);
  and and_1 (and_1_out, en0_out, or_1_out, clk);
  and and_2 (and_2_out, en1_out, or_1_out, clk);
  and and_3 (and_3_out, en2_out, or_1_out, clk);
  and and_4 (and_4_out, en3_out, or_1_out, clk);
  and and_5 (and_5_out, en4_out, or_1_out, clk);
  and and_6 (and_6_out, en5_out, or_1_out, clk);
  and and_7 (and_7_out, en6_out, or_1_out, clk);
  and and_8 (and_8_out, en7_out, or_1_out, clk);
  and and_9 (and_9_out, en8_out, or_1_out, clk);
  and and_10 (and_10_out, en9_out, or_1_out, clk);
  and and_11 (and_11_out, en10_out, or_1_out, clk);
  and and_12 (and_12_out, en11_out, or_1_out, clk);
  and and_13 (and_13_out, en12_out, or_1_out, clk);
  and and_14 (and_14_out, en13_out, or_1_out, clk);
  and and_15 (and_15_out, en14_out, or_1_out, clk);
  and and_16 (and_16_out, en15_out, or_1_out, clk);
  and and_17 (and_17_out, pin_7, program_mode);
  and and_18 (and_18_out, not_5_out, out_7);
  or or_3 (or_3_out, and_17_out, and_18_out);
  memBit membit_1 (.en(en0_out), .dataIn(or_3_out), .clk(and_1_out), .dataOut(membit_1_dataout));
  memBit membit_2 (.en(en1_out), .dataIn(or_3_out), .clk(and_2_out), .dataOut(membit_2_dataout));
  memBit membit_3 (.en(en2_out), .dataIn(or_3_out), .clk(and_3_out), .dataOut(membit_3_dataout));
  memBit membit_4 (.en(en3_out), .dataIn(or_3_out), .clk(and_4_out), .dataOut(membit_4_dataout));
  memBit membit_5 (.en(en4_out), .dataIn(or_3_out), .clk(and_5_out), .dataOut(membit_5_dataout));
  memBit membit_6 (.en(en5_out), .dataIn(or_3_out), .clk(and_6_out), .dataOut(membit_6_dataout));
  memBit membit_7 (.en(en6_out), .dataIn(or_3_out), .clk(and_7_out), .dataOut(membit_7_dataout));
  memBit membit_8 (.en(en7_out), .dataIn(or_3_out), .clk(and_8_out), .dataOut(membit_8_dataout));
  memBit membit_9 (.en(en8_out), .dataIn(or_3_out), .clk(and_9_out), .dataOut(membit_9_dataout));
  memBit membit_10 (.en(en9_out), .dataIn(or_3_out), .clk(and_10_out), .dataOut(membit_10_dataout));
  memBit membit_11 (.en(en10_out), .dataIn(or_3_out), .clk(and_11_out), .dataOut(membit_11_dataout));
  memBit membit_12 (.en(en11_out), .dataIn(or_3_out), .clk(and_12_out), .dataOut(membit_12_dataout));
  memBit membit_13 (.en(en12_out), .clk(and_13_out), .dataOut(membit_13_dataout));  // open: dataIn
  memBit membit_14 (.en(en13_out), .dataIn(or_3_out), .clk(and_14_out), .dataOut(membit_14_dataout));
  memBit membit_15 (.en(en14_out), .dataIn(or_3_out), .clk(and_15_out), .dataOut(membit_15_dataout));
  memBit membit_16 (.en(en15_out), .dataIn(or_3_out), .clk(and_16_out), .dataOut(membit_16_dataout));
  assign out_7 = or_2_out ? or_4_out : 1'bz;  // Controlled_Buffer controlled_buffer_1
  or or_4 (or_4_out, membit_1_dataout, membit_2_dataout, membit_3_dataout, membit_4_dataout, membit_5_dataout, membit_6_dataout, membit_7_dataout, membit_8_dataout, membit_9_dataout, membit_10_dataout, membit_11_dataout, membit_12_dataout, membit_13_dataout, membit_14_dataout, membit_15_dataout, membit_16_dataout);
  and and_19 (and_19_out, pin_6, program_mode);
  and and_20 (and_20_out, not_5_out, out_6);
  or or_5 (or_5_out, and_19_out, and_20_out);
  memBit membit_17 (.en(en0_out), .dataIn(or_5_out), .clk(and_1_out), .dataOut(membit_17_dataout));
  memBit membit_18 (.en(en1_out), .dataIn(or_5_out), .clk(and_2_out), .dataOut(membit_18_dataout));
  memBit membit_19 (.en(en2_out), .dataIn(or_5_out), .clk(and_3_out), .dataOut(membit_19_dataout));
  memBit membit_20 (.en(en3_out), .dataIn(or_5_out), .clk(and_4_out), .dataOut(membit_20_dataout));
  memBit membit_21 (.en(en4_out), .dataIn(or_5_out), .clk(and_5_out), .dataOut(membit_21_dataout));
  memBit membit_22 (.en(en5_out), .dataIn(or_5_out), .clk(and_6_out), .dataOut(membit_22_dataout));
  memBit membit_23 (.en(en6_out), .dataIn(or_5_out), .clk(and_7_out), .dataOut(membit_23_dataout));
  memBit membit_24 (.en(en7_out), .dataIn(or_5_out), .clk(and_8_out), .dataOut(membit_24_dataout));
  memBit membit_25 (.en(en8_out), .dataIn(or_5_out), .clk(and_9_out), .dataOut(membit_25_dataout));
  memBit membit_26 (.en(en9_out), .dataIn(or_5_out), .clk(and_10_out), .dataOut(membit_26_dataout));
  memBit membit_27 (.en(en10_out), .dataIn(or_5_out), .clk(and_11_out), .dataOut(membit_27_dataout));
  memBit membit_28 (.en(en11_out), .dataIn(or_5_out), .clk(and_12_out), .dataOut(membit_28_dataout));
  memBit membit_29 (.en(en12_out), .dataIn(or_5_out), .clk(and_13_out), .dataOut(membit_29_dataout));
  memBit membit_30 (.en(en13_out), .dataIn(or_5_out), .clk(and_14_out), .dataOut(membit_30_dataout));
  memBit membit_31 (.en(en14_out), .dataIn(or_5_out), .clk(and_15_out), .dataOut(membit_31_dataout));
  memBit membit_32 (.en(en15_out), .dataIn(or_5_out), .clk(and_16_out), .dataOut(membit_32_dataout));
  assign out_6 = or_2_out ? or_6_out : 1'bz;  // Controlled_Buffer controlled_buffer_2
  or or_6 (or_6_out, membit_17_dataout, membit_18_dataout, membit_19_dataout, membit_20_dataout, membit_21_dataout, membit_22_dataout, membit_23_dataout, membit_24_dataout, membit_25_dataout, membit_26_dataout, membit_27_dataout, membit_28_dataout, membit_29_dataout, membit_30_dataout, membit_31_dataout, membit_32_dataout);
  and and_21 (and_21_out, pin_5, program_mode);
  and and_22 (and_22_out, not_5_out, out_5);
  or or_7 (or_7_out, and_21_out, and_22_out);
  memBit membit_33 (.en(en0_out), .dataIn(or_7_out), .clk(and_1_out), .dataOut(membit_33_dataout));
  memBit membit_34 (.en(en1_out), .dataIn(or_7_out), .clk(and_2_out), .dataOut(membit_34_dataout));
  memBit membit_35 (.en(en2_out), .dataIn(or_7_out), .clk(and_3_out), .dataOut(membit_35_dataout));
  memBit membit_36 (.en(en3_out), .dataIn(or_7_out), .clk(and_4_out), .dataOut(membit_36_dataout));
  memBit membit_37 (.en(en4_out), .dataIn(or_7_out), .clk(and_5_out), .dataOut(membit_37_dataout));
  memBit membit_38 (.en(en5_out), .dataIn(or_7_out), .clk(and_6_out), .dataOut(membit_38_dataout));
  memBit membit_39 (.en(en6_out), .dataIn(or_7_out), .clk(and_7_out), .dataOut(membit_39_dataout));
  memBit membit_40 (.en(en7_out), .dataIn(or_7_out), .clk(and_8_out), .dataOut(membit_40_dataout));
  memBit membit_41 (.en(en8_out), .dataIn(or_7_out), .clk(and_9_out), .dataOut(membit_41_dataout));
  memBit membit_42 (.en(en9_out), .dataIn(or_7_out), .clk(and_10_out), .dataOut(membit_42_dataout));
  memBit membit_43 (.en(en10_out), .dataIn(or_7_out), .clk(and_11_out), .dataOut(membit_43_dataout));
  memBit membit_44 (.en(en11_out), .dataIn(or_7_out), .clk(and_12_out), .dataOut(membit_44_dataout));
  memBit membit_45 (.en(en12_out), .dataIn(or_7_out), .clk(and_13_out), .dataOut(membit_45_dataout));
  memBit membit_46 (.en(en13_out), .clk(and_14_out), .dataOut(membit_46_dataout));  // open: dataIn
  memBit membit_47 (.en(en14_out), .dataIn(or_7_out), .clk(and_15_out), .dataOut(membit_47_dataout));
  memBit membit_48 (.en(en15_out), .dataIn(or_7_out), .clk(and_16_out), .dataOut(membit_48_dataout));
  assign out_5 = or_2_out ? or_8_out : 1'bz;  // Controlled_Buffer controlled_buffer_3
  or or_8 (or_8_out, membit_33_dataout, membit_34_dataout, membit_35_dataout, membit_36_dataout, membit_37_dataout, membit_38_dataout, membit_39_dataout, membit_40_dataout, membit_41_dataout, membit_42_dataout, membit_43_dataout, membit_44_dataout, membit_45_dataout, membit_46_dataout, membit_47_dataout, membit_48_dataout);
  and and_23 (and_23_out, pin_4, program_mode);
  or or_9 (or_9_out, and_23_out, and_24_out);
  and and_24 (and_24_out, not_5_out, out_4);
  memBit membit_49 (.en(en0_out), .dataIn(or_9_out), .clk(and_1_out), .dataOut(membit_49_dataout));
  memBit membit_50 (.en(en1_out), .dataIn(or_9_out), .clk(and_2_out), .dataOut(membit_50_dataout));
  memBit membit_51 (.en(en2_out), .dataIn(or_9_out), .clk(and_3_out), .dataOut(membit_51_dataout));
  memBit membit_52 (.en(en3_out), .dataIn(or_9_out), .clk(and_4_out), .dataOut(membit_52_dataout));
  memBit membit_53 (.en(en4_out), .dataIn(or_9_out), .clk(and_5_out), .dataOut(membit_53_dataout));
  memBit membit_54 (.en(en5_out), .dataIn(or_9_out), .clk(and_6_out), .dataOut(membit_54_dataout));
  memBit membit_55 (.en(en6_out), .dataIn(or_9_out), .clk(and_7_out), .dataOut(membit_55_dataout));
  memBit membit_56 (.en(en7_out), .dataIn(or_9_out), .clk(and_8_out), .dataOut(membit_56_dataout));
  memBit membit_57 (.en(en8_out), .dataIn(or_9_out), .clk(and_9_out), .dataOut(membit_57_dataout));
  memBit membit_58 (.en(en9_out), .dataIn(or_9_out), .clk(and_10_out), .dataOut(membit_58_dataout));
  memBit membit_59 (.en(en10_out), .dataIn(or_9_out), .clk(and_11_out), .dataOut(membit_59_dataout));
  memBit membit_60 (.en(en11_out), .dataIn(or_9_out), .clk(and_12_out), .dataOut(membit_60_dataout));
  memBit membit_61 (.en(en12_out), .dataIn(or_9_out), .clk(and_13_out), .dataOut(membit_61_dataout));
  memBit membit_62 (.en(en13_out), .dataIn(or_9_out), .clk(and_14_out), .dataOut(membit_62_dataout));
  memBit membit_63 (.en(en14_out), .dataIn(or_9_out), .clk(and_15_out), .dataOut(membit_63_dataout));
  memBit membit_64 (.en(en15_out), .dataIn(or_9_out), .clk(and_16_out), .dataOut(membit_64_dataout));
  assign out_4 = or_2_out ? or_10_out : 1'bz;  // Controlled_Buffer controlled_buffer_4
  or or_10 (or_10_out, membit_49_dataout, membit_50_dataout, membit_51_dataout, membit_52_dataout, membit_53_dataout, membit_54_dataout, membit_55_dataout, membit_56_dataout, membit_57_dataout, membit_58_dataout, membit_59_dataout, membit_60_dataout, membit_61_dataout, membit_62_dataout, membit_63_dataout, membit_64_dataout);
  and and_25 (and_25_out, pin_3, program_mode);
  and and_26 (and_26_out, not_5_out, out_3);
  or or_11 (or_11_out, and_25_out, and_26_out);
  memBit membit_65 (.en(en0_out), .dataIn(or_11_out), .clk(and_1_out), .dataOut(membit_65_dataout));
  memBit membit_66 (.en(en1_out), .dataIn(or_11_out), .clk(and_2_out), .dataOut(membit_66_dataout));
  memBit membit_67 (.en(en2_out), .dataIn(or_11_out), .clk(and_3_out), .dataOut(membit_67_dataout));
  memBit membit_68 (.en(en3_out), .dataIn(or_11_out), .clk(and_4_out), .dataOut(membit_68_dataout));
  memBit membit_69 (.en(en4_out), .dataIn(or_11_out), .clk(and_5_out), .dataOut(membit_69_dataout));
  memBit membit_70 (.en(en5_out), .dataIn(or_11_out), .clk(and_6_out), .dataOut(membit_70_dataout));
  memBit membit_71 (.en(en6_out), .dataIn(or_11_out), .clk(and_7_out), .dataOut(membit_71_dataout));
  memBit membit_72 (.en(en7_out), .clk(and_8_out), .dataOut(membit_72_dataout));  // open: dataIn
  memBit membit_73 (.en(en8_out), .dataIn(or_11_out), .clk(and_9_out), .dataOut(membit_73_dataout));
  memBit membit_74 (.en(en9_out), .dataIn(or_11_out), .clk(and_10_out), .dataOut(membit_74_dataout));
  memBit membit_75 (.en(en10_out), .dataIn(or_11_out), .clk(and_11_out), .dataOut(membit_75_dataout));
  memBit membit_76 (.en(en11_out), .dataIn(or_11_out), .clk(and_12_out), .dataOut(membit_76_dataout));
  memBit membit_77 (.en(en12_out), .dataIn(or_11_out), .clk(and_13_out), .dataOut(membit_77_dataout));
  memBit membit_78 (.en(en13_out), .dataIn(or_11_out), .clk(and_14_out), .dataOut(membit_78_dataout));
  memBit membit_79 (.en(en14_out), .dataIn(or_11_out), .clk(and_15_out), .dataOut(membit_79_dataout));
  memBit membit_80 (.en(en15_out), .dataIn(or_11_out), .clk(and_16_out), .dataOut(membit_80_dataout));
  assign out_3 = or_2_out ? or_12_out : 1'bz;  // Controlled_Buffer controlled_buffer_5
  or or_12 (or_12_out, membit_65_dataout, membit_66_dataout, membit_67_dataout, membit_68_dataout, membit_69_dataout, membit_70_dataout, membit_71_dataout, membit_72_dataout, membit_73_dataout, membit_74_dataout, membit_75_dataout, membit_76_dataout, membit_77_dataout, membit_78_dataout, membit_79_dataout, membit_80_dataout);
  and and_27 (and_27_out, not_5_out, out_2);
  and and_28 (and_28_out, pin_2, program_mode);
  or or_13 (or_13_out, and_28_out, and_27_out);
  memBit membit_81 (.en(en0_out), .dataIn(or_13_out), .clk(and_1_out), .dataOut(membit_81_dataout));
  memBit membit_82 (.en(en1_out), .dataIn(or_13_out), .clk(and_2_out), .dataOut(membit_82_dataout));
  memBit membit_83 (.en(en2_out), .dataIn(or_13_out), .clk(and_3_out), .dataOut(membit_83_dataout));
  memBit membit_84 (.en(en3_out), .dataIn(or_13_out), .clk(and_4_out), .dataOut(membit_84_dataout));
  memBit membit_85 (.en(en4_out), .dataIn(or_13_out), .clk(and_5_out), .dataOut(membit_85_dataout));
  memBit membit_86 (.en(en5_out), .dataIn(or_13_out), .clk(and_6_out), .dataOut(membit_86_dataout));
  memBit membit_87 (.en(en6_out), .dataIn(or_13_out), .clk(and_7_out), .dataOut(membit_87_dataout));
  memBit membit_88 (.en(en7_out), .dataIn(or_13_out), .clk(and_8_out), .dataOut(membit_88_dataout));
  memBit membit_89 (.en(en8_out), .dataIn(or_13_out), .clk(and_9_out), .dataOut(membit_89_dataout));
  memBit membit_90 (.en(en9_out), .dataIn(or_13_out), .clk(and_10_out), .dataOut(membit_90_dataout));
  memBit membit_91 (.en(en10_out), .dataIn(or_13_out), .clk(and_11_out), .dataOut(membit_91_dataout));
  memBit membit_92 (.en(en11_out), .dataIn(or_13_out), .clk(and_12_out), .dataOut(membit_92_dataout));
  memBit membit_93 (.en(en12_out), .dataIn(or_13_out), .clk(and_13_out), .dataOut(membit_93_dataout));
  memBit membit_94 (.en(en13_out), .dataIn(or_13_out), .clk(and_14_out), .dataOut(membit_94_dataout));
  memBit membit_95 (.en(en14_out), .dataIn(or_13_out), .clk(and_15_out), .dataOut(membit_95_dataout));
  memBit membit_96 (.en(en15_out), .dataIn(or_13_out), .clk(and_16_out), .dataOut(membit_96_dataout));
  assign out_2 = or_2_out ? or_14_out : 1'bz;  // Controlled_Buffer controlled_buffer_6
  or or_14 (or_14_out, membit_81_dataout, membit_82_dataout, membit_83_dataout, membit_84_dataout, membit_85_dataout, membit_86_dataout, membit_87_dataout, membit_88_dataout, membit_89_dataout, membit_90_dataout, membit_91_dataout, membit_92_dataout, membit_93_dataout, membit_94_dataout, membit_95_dataout, membit_96_dataout);
  and and_29 (and_29_out, not_5_out, out_1);
  and and_30 (and_30_out, pin_1, program_mode);
  or or_15 (or_15_out, and_30_out, and_29_out);
  memBit membit_97 (.en(en0_out), .dataIn(or_15_out), .clk(and_1_out), .dataOut(membit_97_dataout));
  memBit membit_98 (.en(en1_out), .dataIn(or_15_out), .clk(and_2_out), .dataOut(membit_98_dataout));
  memBit membit_99 (.en(en2_out), .dataIn(or_15_out), .clk(and_3_out), .dataOut(membit_99_dataout));
  memBit membit_100 (.en(en3_out), .dataIn(or_15_out), .clk(and_4_out), .dataOut(membit_100_dataout));
  memBit membit_101 (.en(en4_out), .dataIn(or_15_out), .clk(and_5_out), .dataOut(membit_101_dataout));
  memBit membit_102 (.en(en5_out), .dataIn(or_15_out), .clk(and_6_out), .dataOut(membit_102_dataout));
  memBit membit_103 (.en(en6_out), .dataIn(or_15_out), .clk(and_7_out), .dataOut(membit_103_dataout));
  memBit membit_104 (.en(en7_out), .dataIn(or_15_out), .clk(and_8_out), .dataOut(membit_104_dataout));
  memBit membit_105 (.en(en8_out), .dataIn(or_15_out), .clk(and_9_out), .dataOut(membit_105_dataout));
  memBit membit_106 (.en(en9_out), .dataIn(or_15_out), .clk(and_10_out), .dataOut(membit_106_dataout));
  memBit membit_107 (.en(en10_out), .dataIn(or_15_out), .clk(and_11_out), .dataOut(membit_107_dataout));
  memBit membit_108 (.en(en11_out), .dataIn(or_15_out), .clk(and_12_out), .dataOut(membit_108_dataout));
  memBit membit_109 (.en(en12_out), .dataIn(or_15_out), .clk(and_13_out), .dataOut(membit_109_dataout));
  memBit membit_110 (.en(en13_out), .dataIn(or_15_out), .clk(and_14_out), .dataOut(membit_110_dataout));
  memBit membit_111 (.en(en14_out), .dataIn(or_15_out), .clk(and_15_out), .dataOut(membit_111_dataout));
  memBit membit_112 (.en(en15_out), .dataIn(or_15_out), .clk(and_16_out), .dataOut(membit_112_dataout));
  assign out_1 = or_2_out ? or_16_out : 1'bz;  // Controlled_Buffer controlled_buffer_7
  or or_16 (or_16_out, membit_97_dataout, membit_98_dataout, membit_99_dataout, membit_100_dataout, membit_101_dataout, membit_102_dataout, membit_103_dataout, membit_104_dataout, membit_105_dataout, membit_106_dataout, membit_107_dataout, membit_108_dataout, membit_109_dataout, membit_110_dataout, membit_111_dataout, membit_112_dataout);
  and and_31 (and_31_out, pin_0, program_mode);
  and and_32 (and_32_out, not_5_out, out_0);
  or or_17 (or_17_out, and_31_out, and_32_out);
  memBit membit_113 (.en(en0_out), .dataIn(or_17_out), .clk(and_1_out), .dataOut(membit_113_dataout));
  memBit membit_114 (.en(en1_out), .dataIn(or_17_out), .clk(and_2_out), .dataOut(membit_114_dataout));
  memBit membit_115 (.en(en2_out), .dataIn(or_17_out), .clk(and_3_out), .dataOut(membit_115_dataout));
  memBit membit_116 (.en(en3_out), .dataIn(or_17_out), .clk(and_4_out), .dataOut(membit_116_dataout));
  memBit membit_117 (.en(en4_out), .dataIn(or_17_out), .clk(and_5_out), .dataOut(membit_117_dataout));
  memBit membit_118 (.en(en5_out), .dataIn(or_17_out), .clk(and_6_out), .dataOut(membit_118_dataout));
  memBit membit_119 (.en(en6_out), .dataIn(or_17_out), .clk(and_7_out), .dataOut(membit_119_dataout));
  memBit membit_120 (.en(en7_out), .dataIn(or_17_out), .clk(and_8_out), .dataOut(membit_120_dataout));
  memBit membit_121 (.en(en8_out), .dataIn(or_17_out), .clk(and_9_out), .dataOut(membit_121_dataout));
  memBit membit_122 (.en(en9_out), .dataIn(or_17_out), .clk(and_10_out), .dataOut(membit_122_dataout));
  memBit membit_123 (.en(en10_out), .dataIn(or_17_out), .clk(and_11_out), .dataOut(membit_123_dataout));
  memBit membit_124 (.en(en11_out), .dataIn(or_17_out), .clk(and_12_out), .dataOut(membit_124_dataout));
  memBit membit_125 (.en(en12_out), .dataIn(or_17_out), .clk(and_13_out), .dataOut(membit_125_dataout));
  memBit membit_126 (.en(en13_out), .dataIn(or_17_out), .clk(and_14_out), .dataOut(membit_126_dataout));
  memBit membit_127 (.en(en14_out), .dataIn(or_17_out), .clk(and_15_out), .dataOut(membit_127_dataout));
  memBit membit_128 (.en(en15_out), .dataIn(or_17_out), .clk(and_16_out), .dataOut(membit_128_dataout));
  assign out_0 = or_2_out ? or_18_out : 1'bz;  // Controlled_Buffer controlled_buffer_8
  or or_18 (or_18_out, membit_113_dataout, membit_114_dataout, membit_115_dataout, membit_116_dataout, membit_117_dataout, membit_118_dataout, membit_119_dataout, membit_120_dataout, membit_121_dataout, membit_122_dataout, membit_123_dataout, membit_124_dataout, membit_125_dataout, membit_126_dataout, membit_127_dataout, membit_128_dataout);
endmodule

module memBit (
  input  en,
  input  dataIn,
  input  clk,
  output dataOut
);

  wire d_ff_1_q;

  D_Flip_Flop d_ff_1 (.D(dataIn), .clk(clk), .Q(d_ff_1_q));  // open: Qn, preset, reset
  and and_1 (dataOut, d_ff_1_q, en);
endmodule

module MAR (
  input  program_mode,
  input  clk,
  input  en,
  input  din_3,
  input  pin_3,
  input  din_2,
  input  pin_2,
  input  din_1,
  input  pin_1,
  input  din_0,
  input  pin_0,
  output addr_3,
  output addr_2,
  output addr_1,
  output addr_0
);

  wire and_1_out, and_2_out, and_3_out, and_4_out, and_5_out, and_6_out, and_7_out, and_8_out, and_9_out,
       d_ff_1_q, d_ff_2_q, d_ff_3_q, d_ff_4_q, not_1_out;

  and and_1 (and_1_out, clk, en);
  D_Flip_Flop d_ff_1 (.D(din_3), .clk(and_1_out), .Q(d_ff_1_q));  // open: Qn, preset, reset
  D_Flip_Flop d_ff_2 (.D(din_2), .clk(and_1_out), .Q(d_ff_2_q));  // open: Qn, preset, reset
  D_Flip_Flop d_ff_3 (.D(din_1), .clk(and_1_out), .Q(d_ff_3_q));  // open: Qn, preset, reset
  D_Flip_Flop d_ff_4 (.D(din_0), .clk(and_1_out), .Q(d_ff_4_q));  // open: Qn, preset, reset
  not not_1 (not_1_out, program_mode);
  and and_2 (and_2_out, d_ff_1_q, not_1_out);
  or or_1 (addr_3, and_2_out, and_3_out);
  and and_3 (and_3_out, program_mode, pin_3);
  and and_4 (and_4_out, d_ff_2_q, not_1_out);
  or or_2 (addr_2, and_4_out, and_5_out);
  and and_5 (and_5_out, program_mode, pin_2);
  and and_6 (and_6_out, d_ff_3_q, not_1_out);
  or or_3 (addr_1, and_6_out, and_7_out);
  and and_7 (and_7_out, program_mode, pin_1);
  and and_8 (and_8_out, d_ff_4_q, not_1_out);
  or or_4 (addr_0, and_8_out, and_9_out);
  and and_9 (and_9_out, program_mode, pin_0);
endmodule

module InstructionRegister (
  input  ir_out,
  input  clk,
  input  ir_en,
  input  iin7,
  input  iin6,
  input  iin5,
  input  iin4,
  input  iin3,
  input  iin2,
  input  iin1,
  input  bin0,
  output ir_out_0,
  output ir_out_1,
  output ir_out_2,
  output ir_out_3,
  output ir_out_4,
  output ir_out_5,
  output ir_out_6,
  output ir_out_7,
  output opCode_0,
  output opCode_1,
  output opCode_2,
  output opCode_3
);

  wire and_1_out, d_ff_1_q, d_ff_2_q, d_ff_3_q, d_ff_4_q;

  and and_1 (and_1_out, clk, ir_en);
  D_Flip_Flop d_ff_1 (.D(bin0), .clk(and_1_out), .Q(d_ff_1_q));  // open: Qn, preset, reset
  D_Flip_Flop d_ff_2 (.D(iin1), .clk(and_1_out), .Q(d_ff_2_q));  // open: Qn, preset, reset
  D_Flip_Flop d_ff_3 (.D(iin2), .clk(and_1_out), .Q(d_ff_3_q));  // open: Qn, preset, reset
  D_Flip_Flop d_ff_4 (.D(iin3), .clk(and_1_out), .Q(d_ff_4_q));  // open: Qn, preset, reset
  D_Flip_Flop d_ff_5 (.D(iin4), .clk(and_1_out), .Q(opCode_0));  // open: Qn, preset, reset
  D_Flip_Flop d_ff_6 (.D(iin5), .clk(and_1_out), .Q(opCode_1));  // open: Qn, preset, reset
  D_Flip_Flop d_ff_7 (.D(iin6), .clk(and_1_out), .Q(opCode_2));  // open: Qn, preset, reset
  D_Flip_Flop d_ff_8 (.D(iin7), .clk(and_1_out), .Q(opCode_3));  // open: Qn, preset, reset
  assign ir_out_0 = ir_out ? d_ff_1_q : 1'bz;  // Controlled_Buffer controlled_buffer_1
  assign ir_out_1 = ir_out ? d_ff_2_q : 1'bz;  // Controlled_Buffer controlled_buffer_2
  assign ir_out_2 = ir_out ? d_ff_3_q : 1'bz;  // Controlled_Buffer controlled_buffer_3
  assign ir_out_3 = ir_out ? d_ff_4_q : 1'bz;  // Controlled_Buffer controlled_buffer_4
  assign ir_out_4 = ir_out ? opCode_0 : 1'bz;  // Controlled_Buffer controlled_buffer_5
  assign ir_out_5 = ir_out ? opCode_1 : 1'bz;  // Controlled_Buffer controlled_buffer_6
  assign ir_out_6 = ir_out ? opCode_2 : 1'bz;  // Controlled_Buffer controlled_buffer_7
  assign ir_out_7 = ir_out ? opCode_3 : 1'bz;  // Controlled_Buffer controlled_buffer_8
endmodule

module Controller (
  input  clk,
  input  program_mode,
  input  rst,
  input  op3,
  input  op2,
  input  op1,
  input  op0,
  input  carry_bit,
  output PCout,
  output MARin,
  output RAMout,
  output IRin,
  output PCount_en,
  output ALUin,
  output OUTREGin,
  output AREGin,
  output ALUout,
  output AREGout,
  output HLTclk,
  output BREGin,
  output IRout,
  output RAMin,
  output JMPen
);

  wire and_1_out, and_2_out, and_3_out, and_4_out, and_5_out, and_6_out, and_7_out, d_ff_1_q, d_ff_1_qn,
       d_ff_2_q, d_ff_2_qn, d_ff_3_q, d_ff_3_qn, instructiondecoder_1_aluin, instructiondecoder_1_aluout,
       instructiondecoder_1_aregin, instructiondecoder_1_aregout, instructiondecoder_1_bregin,
       instructiondecoder_1_hltclk, instructiondecoder_1_irout, instructiondecoder_1_jmpen,
       instructiondecoder_1_marin, instructiondecoder_1_outregin, instructiondecoder_1_ramin,
       instructiondecoder_1_ramout, instructiondecoder_1_rstcount, not_1_out, not_2_out, not_3_out,
       not_4_out, not_5_out, or_1_out, or_2_out, or_3_out, or_4_out;

  D_Flip_Flop d_ff_1 (.D(d_ff_1_qn), .clk(not_1_out), .Q(d_ff_1_q), .Qn(d_ff_1_qn), .reset(or_1_out));  // open: preset
  not not_1 (not_1_out, clk);
  or or_1 (or_1_out, rst, or_2_out);
  not not_2 (not_2_out, d_ff_1_q);
  D_Flip_Flop d_ff_2 (.D(d_ff_2_qn), .clk(d_ff_1_qn), .Q(d_ff_2_q), .Qn(d_ff_2_qn), .reset(or_1_out));  // open: preset
  not not_3 (not_3_out, d_ff_2_q);
  D_Flip_Flop d_ff_3 (.D(d_ff_3_qn), .clk(d_ff_2_qn), .Q(d_ff_3_q), .Qn(d_ff_3_qn), .reset(or_1_out));  // open: preset
  not not_4 (not_4_out, d_ff_3_q);
  and and_1 (and_1_out, not_4_out, not_3_out, not_2_out, 1'b1);
  and and_2 (and_2_out, not_4_out, not_3_out, d_ff_1_q, 1'b1);
  and and_3 (and_3_out, not_4_out, d_ff_2_q, not_2_out, 1'b1);
  and and_4 (and_4_out, not_4_out, d_ff_2_q, d_ff_1_q, 1'b1);
  and and_5 (and_5_out, d_ff_3_q, not_3_out, not_2_out, 1'b1);
  and and_6 (and_6_out, d_ff_3_q, not_3_out, d_ff_1_q, 1'b1);
  and and_7 (and_7_out, d_ff_3_q, d_ff_2_q, not_2_out, 1'b1);
  // AND_Gate and_8 has open pins: in0=d_ff_3_q, in1=d_ff_2_q, in2=d_ff_1_q, in3=1'b1, out=open
  InstructionDecoder instructiondecoder_1 (
    .HLTclk(instructiondecoder_1_hltclk), .rstCount(instructiondecoder_1_rstcount), .t5(and_6_out),
    .t4(and_5_out), .t3(and_4_out), .t2(and_3_out), .op3(op3), .op2(op2), .op1(op1), .op0(op0),
    .AREGin(instructiondecoder_1_aregin), .ALUout(instructiondecoder_1_aluout),
    .RAMout(instructiondecoder_1_ramout), .BREGin(instructiondecoder_1_bregin),
    .IRout(instructiondecoder_1_irout), .ALUin(instructiondecoder_1_aluin),
    .OUTREGin(instructiondecoder_1_outregin), .RAMin(instructiondecoder_1_ramin),
    .JMPen(instructiondecoder_1_jmpen), .MARin(instructiondecoder_1_marin),
    .AREGout(instructiondecoder_1_aregout), .carry_bit(carry_bit));
  not not_5 (not_5_out, program_mode);
  or or_2 (or_2_out, instructiondecoder_1_rstcount, and_7_out);
  or or_3 (or_3_out, and_1_out, instructiondecoder_1_marin);
  or or_4 (or_4_out, and_2_out, instructiondecoder_1_ramout);
  assign HLTclk = not_5_out ? instructiondecoder_1_hltclk : 1'bz;  // Controlled_Buffer controlled_buffer_1
  assign BREGin = not_5_out ? instructiondecoder_1_bregin : 1'bz;  // Controlled_Buffer controlled_buffer_2
  assign IRout = not_5_out ? instructiondecoder_1_irout : 1'bz;  // Controlled_Buffer controlled_buffer_3
  assign RAMin = not_5_out ? instructiondecoder_1_ramin : 1'bz;  // Controlled_Buffer controlled_buffer_4
  assign JMPen = not_5_out ? instructiondecoder_1_jmpen : 1'bz;  // Controlled_Buffer controlled_buffer_5
  assign OUTREGin = not_5_out ? instructiondecoder_1_outregin : 1'bz;  // Controlled_Buffer controlled_buffer_6
  assign AREGin = not_5_out ? instructiondecoder_1_aregin : 1'bz;  // Controlled_Buffer controlled_buffer_7
  assign ALUout = not_5_out ? instructiondecoder_1_aluout : 1'bz;  // Controlled_Buffer controlled_buffer_8
  assign AREGout = not_5_out ? instructiondecoder_1_aregout : 1'bz;  // Controlled_Buffer controlled_buffer_9
  assign RAMout = not_5_out ? or_4_out : 1'bz;  // Controlled_Buffer controlled_buffer_10
  assign IRin = not_5_out ? and_2_out : 1'bz;  // Controlled_Buffer controlled_buffer_11
  assign PCount_en = not_5_out ? and_2_out : 1'bz;  // Controlled_Buffer controlled_buffer_12
  assign ALUin = not_5_out ? instructiondecoder_1_aluin : 1'bz;  // Controlled_Buffer controlled_buffer_13
  assign PCout = not_5_out ? and_1_out : 1'bz;  // Controlled_Buffer controlled_buffer_14
  assign MARin = not_5_out ? or_3_out : 1'bz;  // Controlled_Buffer controlled_buffer_15
endmodule

module InstructionDecoder (
  input  carry_bit,
  input  t5,
  input  t4,
  input  t3,
  input  t2,
  input  op3,
  input  op2,
  input  op1,
  input  op0,
  output MARin,
  output AREGin,
  output ALUout,
  output RAMout,
  output BREGin,
  output IRout,
  output ALUin,
  output AREGout,
  output OUTREGin,
  output HLTclk,
  output RAMin,
  output JMPen,
  output rstCount
);

  wire ADD_2_out, ADD_3_out, ADD_4_out, ADD_out, AND_2_out, AND_3_out, AND_4_out, AND_out, HLT_2_out,
       INVB_2_out, INVB_3_out, INVB_out, JC_2_out, JC_3_out, JC_out, JMP_2_out, JMP_out, LDA_2_out,
       LDA_3_out, LDA_out, MOVA_2_out, MOVA_out, not_1_out, not_2_out, not_3_out, not_4_out, not_5_out,
       OR_2_out, OR_3_out, OR_4_out, or_5_out, or_6_out, or_8_out, or_10_out, or_11_out, or_12_out, OR_out,
       OUT_2_out, STA_3_out, STA_out, SUB_2_out, SUB_3_out, SUB_4_out, SUB_out;

  not not_1 (not_1_out, carry_bit);
  not not_2 (not_2_out, op3);
  not not_3 (not_3_out, op2);
  not not_4 (not_4_out, op1);
  not not_5 (not_5_out, op0);
  and LDA (LDA_out, op0, not_4_out, not_3_out, not_2_out, t2);
  and LDA_2 (LDA_2_out, op0, not_4_out, not_3_out, not_2_out, t3);
  and ADD (ADD_out, op0, not_4_out, not_3_out, op3, t2);
  and ADD_2 (ADD_2_out, op0, not_4_out, not_3_out, op3, t3);
  and ADD_3 (ADD_3_out, op0, not_4_out, not_3_out, op3, t4);
  and ADD_4 (ADD_4_out, op0, not_4_out, not_3_out, op3, t5);
  and OUT (OUTREGin, not_5_out, op1, op2, op3, t2);
  and HLT (HLTclk, op0, op1, op2, op3, t2);
  and AND (AND_out, not_5_out, not_4_out, not_3_out, op3, t2);
  and AND_2 (AND_2_out, not_5_out, not_4_out, not_3_out, op3, t3);
  and AND_3 (AND_3_out, not_5_out, not_4_out, not_3_out, op3, t4);
  and AND_4 (AND_4_out, not_5_out, not_4_out, not_3_out, op3, t5);
  and SUB (SUB_out, op0, not_4_out, op2, op3, t2);
  and SUB_2 (SUB_2_out, op0, not_4_out, op2, op3, t3);
  and SUB_3 (SUB_3_out, op0, not_4_out, op2, op3, t4);
  and SUB_4 (SUB_4_out, op0, not_4_out, op2, op3, t5);
  and INVB (INVB_out, op0, op1, not_3_out, op3, t2);
  and INVB_2 (INVB_2_out, op0, op1, not_3_out, op3, t3);
  and OR (OR_out, not_5_out, op1, not_3_out, op3, t2);
  and OR_2 (OR_2_out, not_5_out, op1, not_3_out, op3, t3);
  and OR_3 (OR_3_out, not_5_out, op1, not_3_out, op3, t4);
  and OR_4 (OR_4_out, not_5_out, op1, not_3_out, op3, t5);
  and STA (STA_out, not_5_out, op1, not_3_out, not_2_out, t2);
  and STA_2 (RAMin, not_5_out, op1, not_3_out, not_2_out, t3);
  and MOVA (MOVA_out, op0, op1, not_3_out, not_2_out, t2);
  and JMP (JMP_out, not_5_out, not_4_out, op2, not_2_out, t2);
  and STA_3 (STA_3_out, not_5_out, op1, not_3_out, not_2_out, t4);
  and MOVA_2 (MOVA_2_out, op0, op1, not_3_out, not_2_out, t3);
  and JMP_2 (JMP_2_out, not_5_out, not_4_out, op2, not_2_out, t3);
  and LDA_3 (LDA_3_out, op0, not_4_out, not_3_out, not_2_out, t4);
  and OUT_2 (OUT_2_out, not_5_out, op1, op2, op3, t3);
  and HLT_2 (HLT_2_out, op0, op1, op2, op3, t3);
  and INVB_3 (INVB_3_out, op0, op1, not_3_out, op3, t4);
  and JC (JC_out, op0, not_4_out, op2, not_2_out, t2, not_1_out);
  and JC_2 (JC_2_out, op0, not_4_out, op2, not_2_out, t3);
  and JC_3 (JC_3_out, op0, not_4_out, op2, not_2_out, t2, carry_bit);
  or or_5 (or_5_out, INVB_3_out, or_6_out);
  or or_6 (or_6_out, JC_out, JC_2_out);
  or or_7 (rstCount, STA_3_out, MOVA_2_out, JMP_2_out, LDA_3_out, OUT_2_out, HLT_2_out, or_5_out);
  or or_8 (or_8_out, STA_out, JMP_out, MOVA_out);
  or or_9 (JMPen, JMP_out, JC_3_out);
  or or_10 (or_10_out, ADD_4_out, AND_4_out, SUB_4_out, OR_4_out);
  or or_11 (or_11_out, LDA_out, ADD_out, OR_out, AND_out, SUB_out);
  or or_12 (or_12_out, ADD_2_out, AND_2_out, SUB_2_out, OR_2_out);
  or or_13 (ALUin, ADD_3_out, AND_3_out, SUB_3_out, INVB_out, OR_3_out);
  or or_14 (MARin, STA_out, or_11_out);
  or or_15 (AREGin, or_10_out, MOVA_out, LDA_2_out);
  or or_16 (ALUout, or_10_out, INVB_2_out);
  or or_17 (RAMout, LDA_2_out, or_12_out);
  or or_18 (BREGin, or_12_out, INVB_2_out);
  or or_19 (IRout, or_11_out, or_8_out, ALUin);
  or or_20 (AREGout, OUTREGin, RAMin);
endmodule

module Out_reg (
  input  clk,
  input  out_en,
  input  in7,
  input  in6,
  input  in5,
  input  in4,
  input  in3,
  input  in2,
  input  in1,
  input  in0,
  input  in_11,
  output out_0,
  output out_1,
  output out_2,
  output out_3,
  output out_4,
  output out_5,
  output out_6,
  output out_7
);

  wire and_1_out;

  and and_1 (and_1_out, clk, out_en);
  D_Flip_Flop d_ff_1 (.D(in0), .clk(and_1_out), .Q(out_0), .reset(in_11));  // open: Qn, preset
  D_Flip_Flop d_ff_2 (.D(in1), .clk(and_1_out), .Q(out_1), .reset(in_11));  // open: Qn, preset
  D_Flip_Flop d_ff_3 (.D(in2), .clk(and_1_out), .Q(out_2), .reset(in_11));  // open: Qn, preset
  D_Flip_Flop d_ff_4 (.D(in3), .clk(and_1_out), .Q(out_3), .reset(in_11));  // open: Qn, preset
  D_Flip_Flop d_ff_5 (.D(in4), .clk(and_1_out), .Q(out_4), .reset(in_11));  // open: Qn, preset
  D_Flip_Flop d_ff_6 (.D(in5), .clk(and_1_out), .Q(out_5), .reset(in_11));  // open: Qn, preset
  D_Flip_Flop d_ff_7 (.D(in6), .clk(and_1_out), .Q(out_6), .reset(in_11));  // open: Qn, preset
  D_Flip_Flop d_ff_8 (.D(in7), .clk(and_1_out), .Q(out_7), .reset(in_11));  // open: Qn, preset
endmodule

module test (
  input  in_1,
  input  in_2,
  input  [7:0] in_3
);

  InstructionRegister instructionregister_1 (
    .clk(in_1), .ir_en(in_2), .ir_out_0(in_3[0]), .ir_out_1(in_3[1]), .ir_out_2(in_3[2]), .ir_out_3(in_3[3]),
    .ir_out_4(in_3[4]), .ir_out_5(in_3[5]), .ir_out_6(in_3[6]), .ir_out_7(in_3[7]), .bin0(in_3[0]),
    .iin1(in_3[1]), .iin2(in_3[2]), .iin3(in_3[3]), .iin4(in_3[4]), .iin5(in_3[5]), .iin6(in_3[6]),
    .iin7(in_3[7]));  // open: ir_out, opCode_0, opCode_1, opCode_2, opCode_3
endmodule
